// Logisim project project3.circ as structural Verilog: 2 circuits, main circuit main
// T0
module main (
  output [15:0] out_1
);

  wire and_1_out, and_2_out, and_3_out, and_4_out, and_5_out, and_6_out, and_7_out, and_8_out, and_9_out,
       and_10_out, and_11_out, and_12_out, and_13_out, and_14_out, and_15_out, and_16_out, and_17_out,
       and_18_out, and_19_out, and_20_out, and_21_out, and_22_out, and_23_out, and_24_out, clock_1_out,
       D0_LD, D1_ST, D2_MOV, D3_PSH, D4_PUL, D5_ADD, D6_SUB, D7_DEC, D8_INC, D9_AND, D10_OR, D11_NOT,
       D12_LSL, D13_LSR, D14_BRA, D15_BEQ, D16_BNE, D17_CALL, D18_RET, decoder_4_out0, decoder_4_out1,
       decoder_4_out2, decoder_6_out0, decoder_6_out1, decoder_6_out2, decoder_9_out0, decoder_9_out1,
       decoder_9_out2, decoder_9_out3, decoder_12_out0, decoder_12_out1, decoder_12_out2, decoder_12_out3,
       decoder_13_out0, decoder_13_out1, decoder_14_out0, decoder_14_out1, IR_EN, IR_LH, MEM_CLR, MEM_LD,
       MEM_SEL, MEM_STR, MuxCSel, not_1_out, not_2_out, not_3_out, not_4_out, not_5_out, not_6_out,
       not_7_out, not_8_out, not_9_out, not_10_out, not_11_out, not_12_out, not_13_out, or_1_out, or_2_out,
       SCR, T0, T1, T2, T3, T4, T5, T6, T7;
  wire [1:0] _3RB_FS, _4RB_FS, controlled_buffer_7_out, controlled_buffer_14_out, controlled_buffer_37_out,
       controlled_buffer_42_out, controlled_buffer_44_out, controlled_buffer_64_out,
       controlled_buffer_102_out, controlled_buffer_115_out, controlled_buffer_121_out,
       controlled_buffer_126_out, IR_FS, MuxASel, MuxBSel, OutASel, OutBSel, OutCSel, OutDSel;
  wire [2:0] controlled_buffer_100_out, controlled_buffer_106_out, controlled_buffer_113_out;
  wire [3:0] _3RB_RS, _4RB_RS, ALUFS;

  counter counter_1 (
    .out_2(T0), .out_3(T1), .out_4(T2), .out_5(T3), .out_6(T4), .out_7(T5), .out_8(T6), .out_9(T7), .in_1(SCR));
  and and_1 (and_1_out, D14_BRA, T3);
  assign MuxBSel = and_1_out ? 2'b01 : 2'bz;  // Controlled_Buffer controlled_buffer_1
  assign _3RB_FS = and_1_out ? 2'b01 : 2'bz;  // Controlled_Buffer controlled_buffer_2
  assign _4RB_RS = and_1_out ? 4'b0001 : 4'bz;  // Controlled_Buffer controlled_buffer_3
  assign MEM_SEL = and_1_out ? 1'b0 : 1'bz;  // Controlled_Buffer controlled_buffer_4
  assign MEM_LD = and_1_out ? 1'b0 : 1'bz;  // Controlled_Buffer controlled_buffer_5
  assign MEM_STR = and_1_out ? 1'b0 : 1'bz;  // Controlled_Buffer controlled_buffer_6
  not not_1 (not_1_out, out_1[8]);
  and and_2 (and_2_out, D0_LD, not_1_out, T3);
  assign controlled_buffer_7_out = and_2_out ? out_1[10:9] : 2'bz;  // Controlled_Buffer controlled_buffer_7
  assign MuxASel = and_2_out ? 2'b00 : 2'bz;  // Controlled_Buffer controlled_buffer_8
  assign _4RB_FS = and_2_out ? 2'b01 : 2'bz;  // Controlled_Buffer controlled_buffer_9
  not not_2 (not_2_out, out_1[10]);
  and and_3 (and_3_out, D2_MOV, T3, not_2_out, not_3_out);
  assign OutASel = and_3_out ? out_1[6:5] : 2'bz;  // Controlled_Buffer controlled_buffer_10
  assign MuxCSel = and_3_out ? 1'b1 : 1'bz;  // Controlled_Buffer controlled_buffer_11
  assign ALUFS = and_3_out ? 4'b0000 : 4'bz;  // Controlled_Buffer controlled_buffer_12
  assign MuxASel = and_3_out ? 2'b11 : 2'bz;  // Controlled_Buffer controlled_buffer_13
  Decoder #(.select(2)) decoder_1 (
    .out0(_4RB_RS[0]), .out1(_4RB_RS[1]), .out2(_4RB_RS[2]), .out3(_4RB_RS[3]),
    .sel(controlled_buffer_14_out), .en(and_3_out));
  assign controlled_buffer_14_out = and_3_out ? out_1[9:8] : 2'bz;  // Controlled_Buffer controlled_buffer_14
  assign _4RB_FS = and_3_out ? 2'b01 : 2'bz;  // Controlled_Buffer controlled_buffer_15
  assign MEM_SEL = T0 ? 1'b1 : 1'bz;  // Controlled_Buffer controlled_buffer_16
  assign MEM_LD = T0 ? 1'b1 : 1'bz;  // Controlled_Buffer controlled_buffer_17
  assign _3RB_FS = T0 ? 2'b10 : 2'bz;  // Controlled_Buffer controlled_buffer_18
  assign _3RB_RS = T0 ? 4'b0001 : 4'bz;  // Controlled_Buffer controlled_buffer_19
  assign IR_EN = T0 ? 1'b1 : 1'bz;  // Controlled_Buffer controlled_buffer_20
  assign IR_FS = T0 ? 2'b11 : 2'bz;  // Controlled_Buffer controlled_buffer_21
  assign IR_LH = T0 ? 1'b0 : 1'bz;  // Controlled_Buffer controlled_buffer_22
  assign MEM_STR = T0 ? 1'b0 : 1'bz;  // Controlled_Buffer controlled_buffer_23
  assign OutDSel = T0 ? 2'b00 : 2'bz;  // Controlled_Buffer controlled_buffer_24
  assign MEM_CLR = T0 ? 1'b0 : 1'bz;  // Controlled_Buffer controlled_buffer_25
  Decoder #(.select(5), .enable("false")) decoder_2 (
    .out0(D0_LD), .out1(D1_ST), .out2(D2_MOV), .out3(D3_PSH), .out4(D4_PUL), .out5(D5_ADD), .out6(D6_SUB),
    .out7(D7_DEC), .out8(D8_INC), .out9(D9_AND), .out10(D10_OR), .out11(D11_NOT), .out12(D12_LSL),
    .out13(D13_LSR), .out14(D14_BRA), .out15(D15_BEQ), .out16(D16_BNE), .out17(D17_CALL), .out18(D18_RET),
    .sel(out_1[15:11]));  // open: out19, out20, out21, out22, out23, out24, out25, out26, out27, out28, out29, out30, out31
  Decoder #(.select(2)) decoder_3 (
    .out0(_4RB_RS[0]), .out1(_4RB_RS[1]), .out2(_4RB_RS[2]), .out3(_4RB_RS[3]),
    .sel(controlled_buffer_7_out), .en(and_2_out));
  not not_3 (not_3_out, out_1[7]);
  and and_4 (and_4_out, D14_BRA, T4);
  assign SCR = and_4_out ? 1'b1 : 1'bz;  // Controlled_Buffer controlled_buffer_26
  assign IR_LH = T1 ? 1'b1 : 1'bz;  // Controlled_Buffer controlled_buffer_27
  assign _3RB_RS = T1 ? 4'b0001 : 4'bz;  // Controlled_Buffer controlled_buffer_28
  assign OutDSel = T1 ? 2'b00 : 2'bz;  // Controlled_Buffer controlled_buffer_29
  assign MEM_SEL = T1 ? 1'b1 : 1'bz;  // Controlled_Buffer controlled_buffer_30
  assign MEM_LD = T1 ? 1'b1 : 1'bz;  // Controlled_Buffer controlled_buffer_31
  assign IR_EN = T1 ? 1'b1 : 1'bz;  // Controlled_Buffer controlled_buffer_32
  assign IR_FS = T1 ? 2'b11 : 2'bz;  // Controlled_Buffer controlled_buffer_33
  assign _3RB_FS = T1 ? 2'b10 : 2'bz;  // Controlled_Buffer controlled_buffer_34
  assign MEM_STR = T1 ? 1'b0 : 1'bz;  // Controlled_Buffer controlled_buffer_35
  assign MEM_CLR = T1 ? 1'b0 : 1'bz;  // Controlled_Buffer controlled_buffer_36
  and and_5 (and_5_out, D2_MOV, T3, out_1[10], out_1[7]);
  assign controlled_buffer_37_out = and_5_out ? out_1[6:5] : 2'bz;  // Controlled_Buffer controlled_buffer_37
  assign MuxASel = and_5_out ? 2'b10 : 2'bz;  // Controlled_Buffer controlled_buffer_38
  assign MuxCSel = and_5_out ? 1'b0 : 1'bz;  // Controlled_Buffer controlled_buffer_39
  assign ALUFS = and_5_out ? 4'b0000 : 4'bz;  // Controlled_Buffer controlled_buffer_40
  assign MuxBSel = and_5_out ? 2'b11 : 2'bz;  // Controlled_Buffer controlled_buffer_41
  assign controlled_buffer_42_out = and_5_out ? out_1[9:8] : 2'bz;  // Controlled_Buffer controlled_buffer_42
  assign _3RB_FS = and_5_out ? 2'b01 : 2'bz;  // Controlled_Buffer controlled_buffer_43
  and and_6 (and_6_out, D0_LD, out_1[8], T3);
  assign controlled_buffer_44_out = and_6_out ? out_1[10:9] : 2'bz;  // Controlled_Buffer controlled_buffer_44
  assign MuxASel = and_6_out ? 2'b01 : 2'bz;  // Controlled_Buffer controlled_buffer_45
  assign _4RB_FS = and_6_out ? 2'b01 : 2'bz;  // Controlled_Buffer controlled_buffer_46
  assign OutDSel = and_6_out ? 2'b01 : 2'bz;  // Controlled_Buffer controlled_buffer_47
  Decoder #(.select(2)) decoder_4 (
    .out0(decoder_4_out0), .out1(decoder_4_out1), .out2(decoder_4_out2), .out3(decoder_4_out2),
    .sel(controlled_buffer_42_out), .en(and_5_out));
  assign IR_EN = T2 ? 1'b0 : 1'bz;  // Controlled_Buffer controlled_buffer_48
  Decoder #(.select(2)) decoder_5 (
    .out0(_4RB_RS[0]), .out1(_4RB_RS[1]), .out2(_4RB_RS[2]), .out3(_4RB_RS[3]),
    .sel(controlled_buffer_44_out), .en(and_6_out));
  Decoder #(.select(2)) decoder_6 (
    .out0(decoder_6_out0), .out1(decoder_6_out1), .out2(decoder_6_out2), .out3(decoder_6_out2),
    .sel(controlled_buffer_37_out), .en(and_5_out));
  assign OutCSel = decoder_6_out2 ? 2'b10 : 2'bz;  // Controlled_Buffer controlled_buffer_49
  assign OutCSel = decoder_6_out2 ? 2'b01 : 2'bz;  // Controlled_Buffer controlled_buffer_50
  assign OutCSel = decoder_6_out1 ? 2'b00 : 2'bz;  // Controlled_Buffer controlled_buffer_51
  assign OutCSel = decoder_6_out0 ? 2'b00 : 2'bz;  // Controlled_Buffer controlled_buffer_52
  assign _3RB_RS = decoder_4_out2 ? 4'b0010 : 4'bz;  // Controlled_Buffer controlled_buffer_53
  assign _3RB_RS = decoder_4_out2 ? 4'b0001 : 4'bz;  // Controlled_Buffer controlled_buffer_54
  assign _3RB_RS = decoder_4_out1 ? 4'b0000 : 4'bz;  // Controlled_Buffer controlled_buffer_55
  assign _3RB_RS = decoder_4_out0 ? 4'b0000 : 4'bz;  // Controlled_Buffer controlled_buffer_56
  assign MEM_SEL = D0_LD ? 1'b1 : 1'bz;  // Controlled_Buffer controlled_buffer_57
  assign MEM_LD = D0_LD ? 1'b1 : 1'bz;  // Controlled_Buffer controlled_buffer_58
  assign MEM_STR = D0_LD ? 1'b0 : 1'bz;  // Controlled_Buffer controlled_buffer_59
  assign MEM_SEL = D2_MOV ? 1'b0 : 1'bz;  // Controlled_Buffer controlled_buffer_60
  assign MEM_LD = D2_MOV ? 1'b0 : 1'bz;  // Controlled_Buffer controlled_buffer_61
  assign MEM_STR = D2_MOV ? 1'b0 : 1'bz;  // Controlled_Buffer controlled_buffer_62
  and and_7 (and_7_out, D0_LD, T4);
  assign SCR = and_7_out ? 1'b1 : 1'bz;  // Controlled_Buffer controlled_buffer_63
  Clock clock_1 (.out(clock_1_out));
  part2_main main_1 (
    .OutASel(OutASel), .OutBSel(OutBSel), .FunSel_2(_4RB_FS), .RegSel(_4RB_RS), .MuxASel(MuxASel),
    .OutCSel(OutCSel), .OutDSel(OutDSel), .FunSel_3(_3RB_FS), .RegSel_2(_3RB_RS), .L_H(IR_LH),
    .Enable(IR_EN), .FunSel_4(IR_FS), .MuxCSel(MuxCSel), .MuxBSel(MuxBSel), .FunSel(ALUFS), .in_10(MEM_STR),
    .in_11(MEM_SEL), .in_12(MEM_LD), .in_13(MEM_CLR), .out_23(out_1), .in_2(clock_1_out));  // open: out_21, out_22
  and and_8 (and_8_out, D1_ST, out_1[8], T3);
  Decoder #(.select(2)) decoder_7 (
    .out0(_4RB_RS[0]), .out1(_4RB_RS[1]), .out2(_4RB_RS[2]), .out3(_4RB_RS[3]),
    .sel(controlled_buffer_64_out), .en(and_8_out));
  assign controlled_buffer_64_out = and_8_out ? out_1[10:9] : 2'bz;  // Controlled_Buffer controlled_buffer_64
  assign OutBSel = and_8_out ? out_1[10:9] : 2'bz;  // Controlled_Buffer controlled_buffer_65
  assign ALUFS = and_8_out ? 4'b0000 : 4'bz;  // Controlled_Buffer controlled_buffer_66
  assign OutDSel = and_8_out ? 2'b01 : 2'bz;  // Controlled_Buffer controlled_buffer_67
  Hex_Digit_Display hex_digit_display_1 (.value(out_1[15:12]));  // open: dp
  Hex_Digit_Display hex_digit_display_2 (.value(out_1[11:8]));  // open: dp
  assign MEM_SEL = D1_ST ? 1'b1 : 1'bz;  // Controlled_Buffer controlled_buffer_68
  assign MEM_LD = D1_ST ? 1'b1 : 1'bz;  // Controlled_Buffer controlled_buffer_69
  assign MEM_STR = D1_ST ? 1'b1 : 1'bz;  // Controlled_Buffer controlled_buffer_70
  Hex_Digit_Display hex_digit_display_3 (.value(out_1[7:4]));  // open: dp
  Hex_Digit_Display hex_digit_display_4 (.value(out_1[3:0]));  // open: dp
  and and_9 (and_9_out, D1_ST, T4);
  assign SCR = and_9_out ? 1'b1 : 1'bz;  // Controlled_Buffer controlled_buffer_71
  or or_1 (or_1_out, out_1[2], out_1[3], out_1[4]);
  and and_10 (and_10_out, D5_ADD, T2, out_1[7]);
  not not_4 (not_4_out, or_1_out);
  and and_11 (and_11_out, and_10_out, or_1_out);
  and and_12 (and_12_out, and_10_out, not_4_out);
  assign MuxASel = and_12_out ? 2'b10 : 2'bz;  // Controlled_Buffer controlled_buffer_72
  assign _4RB_FS = and_12_out ? 2'b01 : 2'bz;  // Controlled_Buffer controlled_buffer_73
  assign _4RB_RS = and_12_out ? 4'b0010 : 4'bz;  // Controlled_Buffer controlled_buffer_74
  assign OutCSel = and_12_out ? out_1[6:5] : 2'bz;  // Controlled_Buffer controlled_buffer_75
  assign OutASel = and_12_out ? 2'b10 : 2'bz;  // Controlled_Buffer controlled_buffer_76
  assign MuxASel = and_11_out ? 2'b10 : 2'bz;  // Controlled_Buffer controlled_buffer_77
  assign _4RB_FS = and_11_out ? 2'b01 : 2'bz;  // Controlled_Buffer controlled_buffer_78
  assign OutCSel = and_11_out ? out_1[6:5] : 2'bz;  // Controlled_Buffer controlled_buffer_79
  assign _4RB_RS = and_11_out ? 4'b0001 : 4'bz;  // Controlled_Buffer controlled_buffer_80
  assign OutASel = and_11_out ? 2'b01 : 2'bz;  // Controlled_Buffer controlled_buffer_81
  and and_13 (and_13_out, D5_ADD, T3, out_1[4]);
  or or_2 (or_2_out, out_1[2], out_1[3], out_1[4]);
  not not_5 (not_5_out, or_2_out);
  and and_14 (and_14_out, and_13_out, or_2_out);
  and and_15 (and_15_out, and_13_out, not_5_out);
  assign MuxASel = and_15_out ? 2'b10 : 2'bz;  // Controlled_Buffer controlled_buffer_82
  assign _4RB_FS = and_15_out ? 2'b01 : 2'bz;  // Controlled_Buffer controlled_buffer_83
  assign _4RB_RS = and_15_out ? 4'b0010 : 4'bz;  // Controlled_Buffer controlled_buffer_84
  assign OutCSel = and_15_out ? out_1[6:5] : 2'bz;  // Controlled_Buffer controlled_buffer_85
  assign OutASel = and_15_out ? 2'b10 : 2'bz;  // Controlled_Buffer controlled_buffer_86
  assign MuxASel = and_14_out ? 2'b10 : 2'bz;  // Controlled_Buffer controlled_buffer_87
  assign _4RB_FS = and_14_out ? 2'b01 : 2'bz;  // Controlled_Buffer controlled_buffer_88
  assign OutCSel = and_14_out ? out_1[6:5] : 2'bz;  // Controlled_Buffer controlled_buffer_89
  assign _4RB_RS = and_14_out ? 4'b0001 : 4'bz;  // Controlled_Buffer controlled_buffer_90
  assign OutASel = and_14_out ? 2'b01 : 2'bz;  // Controlled_Buffer controlled_buffer_91
  assign MEM_SEL = D8_INC ? 1'b0 : 1'bz;  // Controlled_Buffer controlled_buffer_92
  assign MEM_LD = D8_INC ? 1'b0 : 1'bz;  // Controlled_Buffer controlled_buffer_93
  assign MEM_STR = D8_INC ? 1'b0 : 1'bz;  // Controlled_Buffer controlled_buffer_94
  assign MEM_CLR = D8_INC ? 1'b0 : 1'bz;  // Controlled_Buffer controlled_buffer_95
  not not_6 (not_6_out, out_1[7]);
  and and_16 (and_16_out, not_6_out, D8_INC, T3, not_7_out);
  assign OutASel = and_16_out ? out_1[6:5] : 2'bz;  // Controlled_Buffer controlled_buffer_96
  assign MuxCSel = and_16_out ? 1'b1 : 1'bz;  // Controlled_Buffer controlled_buffer_97
  assign ALUFS = and_16_out ? 4'b0000 : 4'bz;  // Controlled_Buffer controlled_buffer_98
  assign MuxASel = and_16_out ? 2'b11 : 2'bz;  // Controlled_Buffer controlled_buffer_99
  Decoder #(.select(3)) decoder_8 (
    .out0(_4RB_RS[0]), .out1(_4RB_RS[1]), .out2(_4RB_RS[2]), .out3(_4RB_RS[3]),
    .sel(controlled_buffer_100_out), .en(and_16_out));  // open: out4, out5, out6, out7
  assign controlled_buffer_100_out = and_16_out ? out_1[10:8] : 3'bz;  // Controlled_Buffer controlled_buffer_100
  assign _4RB_FS = and_16_out ? 2'b01 : 2'bz;  // Controlled_Buffer controlled_buffer_101
  and and_17 (and_17_out, out_1[7], D8_INC, T3, not_8_out);
  Decoder #(.select(2)) decoder_9 (
    .out0(decoder_9_out0), .out1(decoder_9_out1), .out2(decoder_9_out2), .out3(decoder_9_out3),
    .sel(controlled_buffer_102_out), .en(and_17_out));
  assign controlled_buffer_102_out = and_17_out ? out_1[6:5] : 2'bz;  // Controlled_Buffer controlled_buffer_102
  assign MuxASel = and_17_out ? 2'b11 : 2'bz;  // Controlled_Buffer controlled_buffer_103
  assign MuxCSel = and_17_out ? 1'b0 : 1'bz;  // Controlled_Buffer controlled_buffer_104
  assign _4RB_FS = and_17_out ? 2'b01 : 2'bz;  // Controlled_Buffer controlled_buffer_105
  assign controlled_buffer_106_out = and_17_out ? out_1[10:8] : 3'bz;  // Controlled_Buffer controlled_buffer_106
  assign _4RB_FS = and_17_out ? 2'b01 : 2'bz;  // Controlled_Buffer controlled_buffer_107
  not not_7 (not_7_out, out_1[10]);
  not not_8 (not_8_out, out_1[10]);
  assign OutCSel = decoder_9_out0 ? 2'b00 : 2'bz;  // Controlled_Buffer controlled_buffer_108
  assign OutCSel = decoder_9_out1 ? 2'b00 : 2'bz;  // Controlled_Buffer controlled_buffer_109
  assign OutCSel = decoder_9_out2 ? 2'b01 : 2'bz;  // Controlled_Buffer controlled_buffer_110
  assign OutCSel = decoder_9_out3 ? 2'b10 : 2'bz;  // Controlled_Buffer controlled_buffer_111
  Decoder #(.select(3)) decoder_10 (
    .out0(_4RB_RS[0]), .out1(_4RB_RS[1]), .out2(_4RB_RS[2]), .out3(_4RB_RS[3]),
    .sel(controlled_buffer_106_out), .en(and_17_out));  // open: out4, out5, out6, out7
  not not_9 (not_9_out, out_1[7]);
  and and_18 (and_18_out, not_9_out, D8_INC, T4, not_10_out);
  assign _4RB_FS = and_18_out ? 2'b10 : 2'bz;  // Controlled_Buffer controlled_buffer_112
  Decoder #(.select(3)) decoder_11 (
    .out0(_4RB_RS[0]), .out1(_4RB_RS[1]), .out2(_4RB_RS[2]), .out3(_4RB_RS[3]),
    .sel(controlled_buffer_113_out), .en(and_18_out));  // open: out4, out5, out6, out7
  assign controlled_buffer_113_out = and_18_out ? out_1[10:8] : 3'bz;  // Controlled_Buffer controlled_buffer_113
  and and_19 (and_19_out, out_1[7], D8_INC, T4, not_11_out);
  assign _4RB_FS = and_19_out ? 2'b10 : 2'bz;  // Controlled_Buffer controlled_buffer_114
  not not_10 (not_10_out, out_1[10]);
  not not_11 (not_11_out, out_1[10]);
  not not_12 (not_12_out, out_1[7]);
  and and_20 (and_20_out, out_1[7], D8_INC, T3, out_1[10]);
  assign controlled_buffer_115_out = and_20_out ? out_1[6:5] : 2'bz;  // Controlled_Buffer controlled_buffer_115
  Decoder #(.select(2)) decoder_12 (
    .out0(decoder_12_out0), .out1(decoder_12_out1), .out2(decoder_12_out2), .out3(decoder_12_out3),
    .sel(controlled_buffer_115_out), .en(and_20_out));
  assign MuxASel = and_20_out ? 2'b10 : 2'bz;  // Controlled_Buffer controlled_buffer_116
  assign MuxCSel = and_20_out ? 1'b0 : 1'bz;  // Controlled_Buffer controlled_buffer_117
  assign ALUFS = and_20_out ? 4'b0000 : 4'bz;  // Controlled_Buffer controlled_buffer_118
  assign MuxBSel = and_20_out ? 2'b11 : 2'bz;  // Controlled_Buffer controlled_buffer_119
  assign _3RB_FS = and_20_out ? 2'b01 : 2'bz;  // Controlled_Buffer controlled_buffer_120
  Decoder #(.select(2)) decoder_13 (
    .out0(decoder_13_out0), .out1(decoder_13_out1), .out2(_3RB_RS[1]), .out3(_3RB_RS[2]),
    .sel(controlled_buffer_121_out), .en(and_20_out));
  assign controlled_buffer_121_out = and_20_out ? out_1[9:8] : 2'bz;  // Controlled_Buffer controlled_buffer_121
  or or_3 (_3RB_RS[0], decoder_13_out0, decoder_13_out1);
  and and_21 (and_21_out, not_12_out, D8_INC, T3, out_1[10]);
  assign OutASel = and_21_out ? out_1[6:5] : 2'bz;  // Controlled_Buffer controlled_buffer_122
  assign MuxCSel = and_21_out ? 1'b1 : 1'bz;  // Controlled_Buffer controlled_buffer_123
  assign ALUFS = and_21_out ? 4'b0000 : 4'bz;  // Controlled_Buffer controlled_buffer_124
  assign MuxBSel = and_21_out ? 2'b11 : 2'bz;  // Controlled_Buffer controlled_buffer_125
  assign controlled_buffer_126_out = and_21_out ? out_1[9:8] : 2'bz;  // Controlled_Buffer controlled_buffer_126
  assign _3RB_FS = and_21_out ? 2'b01 : 2'bz;  // Controlled_Buffer controlled_buffer_127
  assign OutCSel = decoder_12_out0 ? 2'b00 : 2'bz;  // Controlled_Buffer controlled_buffer_128
  assign OutCSel = decoder_12_out1 ? 2'b00 : 2'bz;  // Controlled_Buffer controlled_buffer_129
  assign OutCSel = decoder_12_out2 ? 2'b01 : 2'bz;  // Controlled_Buffer controlled_buffer_130
  assign OutCSel = decoder_12_out3 ? 2'b10 : 2'bz;  // Controlled_Buffer controlled_buffer_131
  Decoder #(.select(2)) decoder_14 (
    .out0(decoder_14_out0), .out1(decoder_14_out1), .out2(_3RB_RS[1]), .out3(_3RB_RS[2]),
    .sel(controlled_buffer_126_out), .en(and_21_out));
  or or_4 (_3RB_RS[0], decoder_14_out0, decoder_14_out1);
  not not_13 (not_13_out, out_1[7]);
  and and_22 (and_22_out, out_1[7], D8_INC, T4, out_1[10]);
  assign _3RB_FS = and_22_out ? 2'b10 : 2'bz;  // Controlled_Buffer controlled_buffer_132
  and and_23 (and_23_out, not_13_out, D8_INC, T4, out_1[10]);
  assign _3RB_FS = and_23_out ? 2'b10 : 2'bz;  // Controlled_Buffer controlled_buffer_133
  and and_24 (and_24_out, D8_INC, T5);
  assign SCR = and_24_out ? 1'b1 : 1'bz;  // Controlled_Buffer controlled_buffer_134

  // Other names for the same wires on the sheet: ADDRESS[7:0] = out_1[7:0]; INSTR[15:0] = out_1;
  //   SRCREG2[2:0] = out_1[4:2]; SRCREG1[2:0] = out_1[7:5]; AdrMOD = out_1[8]; DESTREG[2:0] = out_1[10:8];
  //   REGSEL[1:0] = out_1[10:9]; OPCODE[4:0] = out_1[15:11]

  // Notes on the sheet:
  //   MOV
  //   BRA
  //   LD
  //   ST
  //   ADD
  //   4RB TO 4RB
  //   3RB TO 4RB
  //   INC
  //   3RB TO 3RB
  //   4RB TO 3RB
endmodule

module counter (
  input  in_1,
  output out_2,
  output out_3,
  output out_4,
  output out_5,
  output out_6,
  output out_7,
  output out_8,
  output out_9
);

  wire clock_1_out;
  wire [2:0] counter_1_q;

  Counter #(.width(3), .max('h7)) counter_1 (
    .Q(counter_1_q), .clk(clock_1_out), .clr(in_1));  // open: load, D, count, carry
  Clock clock_1 (.out(clock_1_out));
  Decoder #(.select(3), .enable("false")) decoder_1 (
    .out0(out_2), .out1(out_3), .out2(out_4), .out3(out_5), .out4(out_6), .out5(out_7), .out6(out_8),
    .out7(out_9), .sel(counter_1_q));
endmodule
